# Fritzing sketch Untitled Sketch 2 (saved by Fritzing 0.9.3b)
breadboards: 1

parts:
  Деталь1 = Arduino Uno (Rev3)
  RHT1 = Humidity and Temperature Sensor RHT03
  SIM800L_BO1 = SIM800L BO
  R1 = Resistor [tolerance=±5% resistance=10k package=THT]
  LED1 = RGB LED (com. cathode, rgb) [package="5 mm [THT]"]
  R2 = Resistor [tolerance=±5% resistance=220 package=THT]
  R3 = Resistor [tolerance=±5% resistance=220 package=THT]
  R4 = Resistor [tolerance=±5% resistance=220 package=THT]
  ANT1 = Antenna
  Reg1 = DC-DC CONVERTER [part_number=80633 package=dc-dc_converter]
  VCC1 = Battery

nets:
  N1: Деталь1.A0, RHT1.GND_1
  N2: Деталь1.D8, SIM800L_BO1.pin_4
  N3: Деталь1.D9_PWM, SIM800L_BO1.pin_5
  N4: Деталь1.D2, LED1.green_anode, R4.Pin_0, R4.Pin_1
  N5: Деталь1.D3_PWM, LED1.blue_anode, R3.Pin_0, R3.Pin_1
  N6: Деталь1.D4, LED1.red_anode, R2.Pin_0, R2.Pin_1
  5V: Деталь1.5V, RHT1.Vcc, R1.Pin_1
  N7: RHT1.Data-signal, R1.Pin_0
  N8: RHT1.GND_2, LED1.common_cathode
  N9: SIM800L_BO1.PIN1, ANT1.antenna_lead
  N10: SIM800L_BO1.PIN2, Reg1.OUT+
  N11: SIM800L_BO1.pin_6, Reg1.OUT-
  N12: Reg1.IN-, VCC1.-
  N13: Reg1.IN+, VCC1.+

custom parts:
  DC-DC CONVERTER: WYHP 5A constant current/voltage manufactured by Shenzhen Weiyapuhua Technology Co., Ltd
